# Fritzing sketch Hauptschaltplan (saved by Fritzing 1.0.6)
breadboards: 1

parts:
  A1 = Arduino UNO R4 WiFi
  M2 = E18-D80NK_1 [package=THT]
  M3 = DC Motor [voltage_(max)=6V voltage_(min)=3V]
  V1 = DC Power Supply [voltage=12V internal_resistance=1Ω max_current=0.1A]
  R1 = Rotary Potentiometer (Small) [maximum_resistance=10kΩ knob_status=50% power=0.5W package=THT]
  M1 = E18-D80NK_1 [package=THT]
  LCD2004-I2C1 = LCD2004-I2C
  R2 = Resistor [tolerance=±5% power=0.25W resistance=10000 package=THT]
  S3 = Taiway 100-SP-X-T1 SPDT Miniature Toggle Switch [part_number=100-SP-X-T1-0-0-B1-M1 package=THT]
  R3 = Resistor [tolerance=±5% power=0.25W resistance=10000 package=THT]
  A2 = drv-1012
  D1 = Zener Diode [part_number=1N4732A breakdown_voltage=12.1V package="300 mil [THT]"]
  D2 = Zener Diode [part_number=1N4732A breakdown_voltage=12.1V package="300 mil [THT]"]
  S6 = Pushbutton [package=THT]
  S7 = Pushbutton [package=THT]
  S8 = DIP Switch 3 Position
  C2 = Electrolytic Capacitor [capacitance=1µF voltage=35V package="100 mil [THT, electrolytic]"]
  R4 = Resistor [tolerance=±5% power=0.25W resistance=47 package=THT]
  C3 = Electrolytic Capacitor [capacitance=1µF voltage=35V package="100 mil [THT, electrolytic]"]

nets:
  N1: A1.Pin_2, A1.Pin_9, A1.Pin_10, A1.Pin_25, A1.Pin_30, M2.pin1, R1.leg2, M1.pin1, LCD2004-I2C1.GND, A2.Pin_1, D1.anode, D2.anode, S6.leg0, S7.leg0, S8.4, S8.5, S8.6, C3.-
  N2: A1.Pin_8, A1.Pin_27, M2.pin2, R1.leg1, M1.pin2, LCD2004-I2C1.VCC, R2.Pin_1, R3.Pin_1, A2.Pin_3, A2.Pin_7
  N3: A1.Pin_11, D1.cathode, D2.cathode, R4.Pin_1, C3.+
  N4: A1.Pin_12, R1.wiper
  N5: A1.Pin_36, M1.pin3, R2.Pin_0
  N6: A1.Pin_38, M2.pin3, R3.Pin_0
  N7: A1.Pin_39, A2.Pin_4
  N8: A1.Pin_40, A2.Pin_8
  N9: A1.Pin_41, S7.leg1
  N10: A1.Pin_42, S6.leg1
  N11: A1.Pin_43, S8.3
  N12: A1.Pin_44, S8.2
  N13: A1.Pin_45, S8.1
  N14: A1.Pin_46, LCD2004-I2C1.SDA
  N15: A1.Pin_47, LCD2004-I2C1.SCL
  N16: M3.pin_1, A2.Pin_10
  N17: M3.pin_2, A2.Pin_9
  N18: V1.Pin_2, A2.Pin_12, C2.+
  N19: V1.Pin_1, S3.COM
  N20: S3.L2, A2.Pin_11, C2.-
  N21: A2.Pin_5, R4.Pin_0

custom parts:
  Arduino UNO R4 WiFi: The Arduino UNO R4 WiFi merges the RA4M1 microprocessor from Renesas with the ESP32-S3 from Espressif, creating an all-in-one tool for makers with enhanced processing power and a diverse array of new peripherals.
  E18-D80NK_1: E18-D80NK Proximity Sensor module.
  LCD2004-I2C: A standard character display with 4x20 characters. Comes in many colors with LCM2004 IIC attached.
  drv-1012: .The BTS7960 is a fully integrated high current H bridge module for motor drive applications.
